// Logisim project ESF.circ as structural Verilog
module S_box_0 (
  input  [3:0] in_1,
  output [3:0] out_2
);

  Multiplexer #(.select(4), .width(4), .enable("false")) multiplexer_1 (
    .in0(4'b0011), .in1(4'b1000), .in2(4'b1111), .in3(4'b0001), .in4(4'b1010), .in5(4'b0110), .in6(4'b0101),
    .in7(4'b1011), .in8(4'b1110), .in9(4'b1101), .in10(4'b0100), .in11(4'b0010), .in12(4'b0111),
    .in13(4'b0000), .in14(4'b1001), .in15(4'b1100), .out(out_2), .sel(in_1));
endmodule

module S_box_1 (
  input  [3:0] in_1,
  output [3:0] out_2
);

  Multiplexer #(.select(4), .width(4), .enable("false")) multiplexer_1 (
    .in0(4'b1111), .in1(4'b1100), .in2(4'b0010), .in3(4'b0111), .in4(4'b1001), .in5(4'b0000), .in6(4'b0101),
    .in7(4'b1010), .in8(4'b0001), .in9(4'b1011), .in10(4'b1110), .in11(4'b1000), .in12(4'b0110),
    .in13(4'b1101), .in14(4'b0011), .in15(4'b0100), .out(out_2), .sel(in_1));
endmodule

module S_box_2 (
  input  [3:0] in_1,
  output [3:0] out_2
);

  Multiplexer #(.select(4), .width(4), .enable("false")) multiplexer_1 (
    .in0(4'b1000), .in1(4'b0110), .in2(4'b0111), .in3(4'b1001), .in4(4'b0011), .in5(4'b1100), .in6(4'b1010),
    .in7(4'b1111), .in8(4'b1101), .in9(4'b0001), .in10(4'b1110), .in11(4'b0100), .in12(4'b0000),
    .in13(4'b1011), .in14(4'b0101), .in15(4'b0010), .out(out_2), .sel(in_1));
endmodule

module S_box_3 (
  input  [3:0] in_1,
  output [3:0] out_2
);

  Multiplexer #(.select(4), .width(4), .enable("false")) multiplexer_1 (
    .in0(4'b0000), .in1(4'b1111), .in2(4'b1011), .in3(4'b1000), .in4(4'b1100), .in5(4'b1001), .in6(4'b0110),
    .in7(4'b0011), .in8(4'b1101), .in9(4'b0001), .in10(4'b0010), .in11(4'b0100), .in12(4'b1010),
    .in13(4'b0111), .in14(4'b0101), .in15(4'b1110), .out(out_2), .sel(in_1));
endmodule

module S_box_4 (
  input  [3:0] in_1,
  output [3:0] out_2
);

  Multiplexer #(.select(4), .width(4), .enable("false")) multiplexer_1 (
    .in0(4'b0001), .in1(4'b1111), .in2(4'b1000), .in3(4'b0011), .in4(4'b1100), .in5(4'b0000), .in6(4'b1011),
    .in7(4'b0110), .in8(4'b0010), .in9(4'b0101), .in10(4'b0100), .in11(4'b1010), .in12(4'b1001),
    .in13(4'b1110), .in14(4'b0111), .in15(4'b1101), .out(out_2), .sel(in_1));
endmodule

module S_box_5 (
  input  [3:0] in_1,
  output [3:0] out_2
);

  Multiplexer #(.select(4), .width(4), .enable("false")) multiplexer_1 (
    .in0(4'b1111), .in1(4'b0101), .in2(4'b0010), .in3(4'b1011), .in4(4'b0100), .in5(4'b1010), .in6(4'b1001),
    .in7(4'b1100), .in8(4'b0000), .in9(4'b0011), .in10(4'b1110), .in11(4'b1000), .in12(4'b1101),
    .in13(4'b0110), .in14(4'b0111), .in15(4'b0001), .out(out_2), .sel(in_1));
endmodule

module S_box_6 (
  input  [3:0] in_1,
  output [3:0] out_2
);

  Multiplexer #(.select(4), .width(4), .enable("false")) multiplexer_1 (
    .in0(4'b0111), .in1(4'b0010), .in2(4'b1100), .in3(4'b0101), .in4(4'b1000), .in5(4'b0100), .in6(4'b0110),
    .in7(4'b1011), .in8(4'b1110), .in9(4'b1001), .in10(4'b0001), .in11(4'b1111), .in12(4'b1101),
    .in13(4'b0011), .in14(4'b1010), .in15(4'b0000), .out(out_2), .sel(in_1));
endmodule

module S_box_7 (
  input  [3:0] in_1,
  output [3:0] out_2
);

  Multiplexer #(.select(4), .width(4), .enable("false")) multiplexer_1 (
    .in0(4'b0001), .in1(4'b1101), .in2(4'b1111), .in3(4'b0000), .in4(4'b1110), .in5(4'b1000), .in6(4'b0010),
    .in7(4'b1011), .in8(4'b0111), .in9(4'b0100), .in10(4'b1100), .in11(4'b1010), .in12(4'b1001),
    .in13(4'b0011), .in14(4'b0101), .in15(4'b0110), .out(out_2), .sel(in_1));
endmodule
